// Logisim project proje.circ as structural Verilog: 6 circuits, main circuit main
module main (
);

  wire ALU_zero, and_1_out, and_2_out, clk_out, CONTROL_UNIT_alusrc, CONTROL_UNIT_beq, CONTROL_UNIT_bneq,
       CONTROL_UNIT_memread, CONTROL_UNIT_memtoreg, CONTROL_UNIT_memwrite, CONTROL_UNIT_regwrite, not_1_out,
       or_1_out;
  wire [1:0] CONTROL_UNIT_aluop;
  wire [4:0] rom_1_data;
  wire [15:0] adder_1_out, adder_2_out, ALU_alu_result, bit_extender_1_out, multiplexer_1_out,
       multiplexer_2_out, multiplexer_3_out, PC_q, ram_1_data, REGFILE_readdata1, REGFILE_readdata2,
       shifter_1_out;
  wire [15:5] rom_1_data_2;

  Register #(.width(16)) PC (.D(multiplexer_2_out), .en(1'b1), .Q(PC_q), .clk(clk_out));  // open: clr
  Adder #(.width(16)) adder_1 (.a(PC_q), .b(16'h1), .out(adder_1_out));  // open: cin, cout
  ROM #(.dataWidth(16)) rom_1 (.addr(PC_q[7:0]), .data({rom_1_data_2, rom_1_data}));  // open: sel
  Clock clk (.out(clk_out));
  assign bit_extender_1_out = {{11{rom_1_data[4]}}, rom_1_data};  // Bit_Extender bit_extender_1
  RegisterFile REGFILE (
    .WriteData(multiplexer_3_out), .RegWrite(CONTROL_UNIT_regwrite), .WriteRegister(rom_1_data_2[10:8]),
    .clk(clk_out), .ReadRegister1(rom_1_data_2[7:5]), .ReadRegister2(rom_1_data_2[10:8]),
    .ReadData1(REGFILE_readdata1), .ReadData2(REGFILE_readdata2));
  Shifter #(.width(16), .shift("ar")) shifter_1 (.in(bit_extender_1_out), .\dist (4'b0001), .out(shifter_1_out));
  Multiplexer #(.width(16), .disabled(0), .enable("false")) multiplexer_1 (
    .in0(REGFILE_readdata2), .in1(bit_extender_1_out), .out(multiplexer_1_out), .sel(CONTROL_UNIT_alusrc));
  ControlUnit CONTROL_UNIT (
    .Opcode(rom_1_data_2[15:11]), .RegWrite(CONTROL_UNIT_regwrite), .AluSrc(CONTROL_UNIT_alusrc),
    .MemRead(CONTROL_UNIT_memread), .MemToReg(CONTROL_UNIT_memtoreg), .BEQ(CONTROL_UNIT_beq),
    .MemWrite(CONTROL_UNIT_memwrite), .BNEQ(CONTROL_UNIT_bneq), .AluOp(CONTROL_UNIT_aluop));
  Adder #(.width(16)) adder_2 (.a(PC_q), .b(shifter_1_out), .out(adder_2_out));  // open: cin, cout
  ALU ALU (
    .A_in(REGFILE_readdata1), .B_in(multiplexer_1_out), .AluOP(CONTROL_UNIT_aluop),
    .Alu_result(ALU_alu_result), .Zero(ALU_zero));
  not not_1 (not_1_out, ALU_zero);
  and and_1 (and_1_out, ALU_zero, CONTROL_UNIT_beq);
  and and_2 (and_2_out, not_1_out, CONTROL_UNIT_bneq);
  RAM #(.addrWidth(4), .dataWidth(16), .bus("separate")) ram_1 (
    .addr(ALU_alu_result[3:0]), .din(REGFILE_readdata2), .data(ram_1_data), .str(CONTROL_UNIT_memwrite),
    .clk(clk_out), .ld(CONTROL_UNIT_memread));  // open: sel, clr
  or or_1 (or_1_out, and_1_out, and_2_out);
  Multiplexer #(.width(16), .disabled(0), .enable("false")) multiplexer_2 (
    .in0(adder_1_out), .in1(adder_2_out), .out(multiplexer_2_out), .sel(or_1_out));
  Multiplexer #(.width(16), .disabled(0), .enable("false")) multiplexer_3 (
    .in0(ALU_alu_result), .in1(ram_1_data), .out(multiplexer_3_out), .sel(CONTROL_UNIT_memtoreg));

  // Notes on the sheet:
  //   contents of rom_1 (hex, n*v repeats v):
  //   100 200 304 2440 e85 3e04 121 241 3a76 2904
  //   LSB
  //   MSB
endmodule

module RegisterFile (
  input  [2:0] ReadRegister1,
  input  RegWrite,
  input  [2:0] WriteRegister,
  input  [15:0] WriteData,
  input  clk,
  input  [2:0] ReadRegister2,
  output [15:0] ReadData1,
  output [15:0] ReadData2
);

  wire demultiplexer_1_out0, demultiplexer_1_out1, demultiplexer_1_out2, demultiplexer_1_out3,
       demultiplexer_1_out4, demultiplexer_1_out5, demultiplexer_1_out6, demultiplexer_1_out7;
  wire [15:0] R0_q, R1_q, R2_q, R3_q, R4_q, R5_q, R6_q, R7_q;

  Demultiplexer #(.select(3), .disabled(0), .enable("false")) demultiplexer_1 (
    .out0(demultiplexer_1_out0), .out1(demultiplexer_1_out1), .out2(demultiplexer_1_out2),
    .out3(demultiplexer_1_out3), .out4(demultiplexer_1_out4), .out5(demultiplexer_1_out5),
    .out6(demultiplexer_1_out6), .out7(demultiplexer_1_out7), .in(RegWrite), .sel(WriteRegister));
  Register #(.width(16)) R0 (.D(WriteData), .en(demultiplexer_1_out0), .Q(R0_q), .clk(clk));  // open: clr
  Register #(.width(16)) R1 (.D(WriteData), .en(demultiplexer_1_out1), .Q(R1_q), .clk(clk));  // open: clr
  Register #(.width(16)) R2 (.D(WriteData), .en(demultiplexer_1_out2), .Q(R2_q), .clk(clk));  // open: clr
  Register #(.width(16)) R3 (.D(WriteData), .en(demultiplexer_1_out3), .Q(R3_q), .clk(clk));  // open: clr
  Register #(.width(16)) R4 (.D(WriteData), .en(demultiplexer_1_out4), .Q(R4_q), .clk(clk));  // open: clr
  Register #(.width(16)) R5 (.D(WriteData), .en(demultiplexer_1_out5), .Q(R5_q), .clk(clk));  // open: clr
  Register #(.width(16)) R6 (.D(WriteData), .en(demultiplexer_1_out6), .Q(R6_q), .clk(clk));  // open: clr
  Register #(.width(16)) R7 (.D(WriteData), .en(demultiplexer_1_out7), .Q(R7_q), .clk(clk));  // open: clr
  Multiplexer #(.select(3), .width(16), .enable("false")) multiplexer_1 (
    .in0(R0_q), .in1(R1_q), .in2(R2_q), .in3(R3_q), .in4(R4_q), .in5(R5_q), .in6(R6_q), .in7(R7_q),
    .out(ReadData1), .sel(ReadRegister1));
  Multiplexer #(.select(3), .width(16), .enable("false")) multiplexer_2 (
    .in0(R0_q), .in1(R1_q), .in2(R2_q), .in3(R3_q), .in4(R4_q), .in5(R5_q), .in6(R6_q), .in7(R7_q),
    .out(ReadData2), .sel(ReadRegister2));
endmodule

module ALU (
  input  [15:0] A_in,
  input  [15:0] B_in,
  input  [1:0] AluOP,
  output [15:0] Alu_result,
  output Zero
);

  wire [15:0] adder_1_out, and_1_out, or_1_out, subtractor_1_out;

  Adder #(.width(16)) adder_1 (.a(A_in), .b(B_in), .out(adder_1_out));  // open: cin, cout
  Subtractor #(.width(16)) subtractor_1 (.a(A_in), .b(B_in), .out(subtractor_1_out));  // open: bin, bout
  assign and_1_out = A_in & B_in;  // AND_Gate and_1, 16 bits wide
  assign or_1_out = A_in | B_in;  // OR_Gate or_1, 16 bits wide
  Multiplexer #(.select(2), .width(16)) multiplexer_1 (
    .in0(adder_1_out), .in1(subtractor_1_out), .in2(and_1_out), .in3(or_1_out), .out(Alu_result), .sel(AluOP));  // open: en
  nor nor_1 (Zero, Alu_result[0], Alu_result[1], Alu_result[2], Alu_result[3], Alu_result[4], Alu_result[5], Alu_result[6], Alu_result[7], Alu_result[8], Alu_result[9], Alu_result[10], Alu_result[11], Alu_result[12], Alu_result[13], Alu_result[14], Alu_result[15]);
endmodule

module ControlUnit (
  input  [4:0] Opcode,
  output RegWrite,
  output AluSrc,
  output MemRead,
  output MemToReg,
  output BEQ,
  output MemWrite,
  output BNEQ,
  output [1:0] AluOp
);

  wire ADDI_out, ANDI_out, ORI_out, SUBI_out;

  and ADDI (ADDI_out, ~Opcode[0], ~Opcode[1], ~Opcode[2], ~Opcode[3], ~Opcode[4]);  // AND_Gate
  and SUBI (SUBI_out, Opcode[0], ~Opcode[1], ~Opcode[2], ~Opcode[3], ~Opcode[4]);  // AND_Gate
  and ANDI (ANDI_out, ~Opcode[0], Opcode[1], ~Opcode[2], ~Opcode[3], ~Opcode[4]);  // AND_Gate
  and ORI (ORI_out, Opcode[0], Opcode[1], ~Opcode[2], ~Opcode[3], ~Opcode[4]);  // AND_Gate
  and LDR (MemRead, ~Opcode[0], ~Opcode[1], Opcode[2], ~Opcode[3], ~Opcode[4]);  // AND_Gate
  and STR (MemWrite, Opcode[0], ~Opcode[1], Opcode[2], ~Opcode[3], ~Opcode[4]);  // AND_Gate
  and u_BEQ (BEQ, ~Opcode[0], Opcode[1], Opcode[2], ~Opcode[3], ~Opcode[4]);  // AND_Gate
  and BNE (BNEQ, Opcode[0], Opcode[1], Opcode[2], ~Opcode[3], ~Opcode[4]);  // AND_Gate
  or or_1 (RegWrite, ADDI_out, SUBI_out, ANDI_out, ORI_out, MemRead);
  or or_2 (AluSrc, ADDI_out, SUBI_out, ANDI_out, ORI_out, MemRead, MemWrite);
  or or_3 (AluOp[0], SUBI_out, BEQ, BNEQ, ORI_out);
  or or_4 (AluOp[1], ANDI_out, ORI_out);

  assign MemToReg = MemRead;

  // Notes on the sheet:
  //   0 -> LSB
  //   negate 1 -> LSB
  //   00000 : ADD
  //   00001 : SUB
  //   00010 : AND
  //   00011 : OR
  //   00100 : LDR
  //   00101 : STR
  //   00110 : BEQ
  //   00111 : BNEQ
endmodule

module PC (
  input  PcSrc,
  input  [15:0] BranchAddr,
  input  clk,
  output [15:0] PcOut
);

  wire [15:0] adder_1_out, multiplexer_1_out;

  Register #(.width(16)) PC (.D(multiplexer_1_out), .en(1'b1), .Q(PcOut), .clk(clk));  // open: clr
  Adder #(.width(16)) adder_1 (.a(PcOut), .b(16'h2), .out(adder_1_out));  // open: cin, cout
  Multiplexer #(.width(16), .enable("false")) multiplexer_1 (
    .in0(adder_1_out), .in1(BranchAddr), .out(multiplexer_1_out), .sel(PcSrc));
endmodule

module FETCH (
  input  clk,
  input  reset,
  input  [15:0] PC_Plus_1,
  input  [15:0] Branch_Target,
  input  PcSrc,
  output [15:0] Instruction
);

  wire [15:0] multiplexer_1_out, PC_q;

  Multiplexer #(.width(16)) multiplexer_1 (
    .in0(PC_Plus_1), .in1(Branch_Target), .out(multiplexer_1_out), .sel(PcSrc));  // open: en
  Register #(.width(16)) PC (.D(multiplexer_1_out), .en(1'b1), .Q(PC_q), .clk(clk), .clr(reset));
  Adder #(.width(16)) adder_1 (.a(PC_q), .b(16'h1), .out(PC_Plus_1));  // open: cin, cout
  ROM #(.dataWidth(16)) rom_1 (.addr(PC_q[7:0]), .data(Instruction));  // open: sel

  // Notes on the sheet:
  //   contents of rom_1 (hex, n*v repeats v):
  //   200 405 60a a04 2460 3904 221 661 da1 3a92 289f
endmodule
